# Fritzing sketch Exp_08_hello_clock (saved by Fritzing 0.9.3b)
breadboards: 1

parts:
  S1 = Pushbutton [package="[THT]"]
  S2 = Pushbutton [package="[THT]"]
  S3 = Pushbutton [package="[THT]"]
  R1 = Resistor [tolerance=±5% resistance=1k package=THT]
  R2 = Resistor [tolerance=±5% resistance=1k package=THT]
  R3 = Resistor [tolerance=±5% resistance=1k package=THT]
  Launchpad1 = TI Launchpad MSP430G2

nets:
  GND: S1.Pin_1, S1.Pin_2, S2.Pin_1, S2.Pin_2, S3.Pin_1, S3.Pin_2
  N1: S1.Pin_3, S1.Pin_4, R1.Pin_1, Launchpad1.p6
  N2: S2.Pin_3, S2.Pin_4, R2.Pin_1, Launchpad1.p15
  N3: S3.Pin_3, S3.Pin_4, R3.Pin_1, Launchpad1.p14
  3.3V: R1.Pin_0, R2.Pin_0, R3.Pin_0
